# Fritzing sketch Sensor Circut and Shematic (saved by Fritzing 0.9.3b)
breadboards: 1

parts:
  LED1 = LED - 5mm [color="Red (633nm)" package="5 mm [THT]"]
  R1 = Resistor [tolerance=±5% resistance=1k package=THT]
  R2 = Resistor [tolerance=±5% resistance=2.2k package=THT]
  Part1 = Arduino Uno (Rev3)
  R3 = Photocell (LDR) [package=THT]

nets:
  N1: LED1.cathode, R1.Pin_0, Part1.D9_PWM
  N2: LED1.anode, R2.Pin_1, Part1.GND
  N3: R2.Pin_0, Part1.A0, R3.pin_1
  N4: Part1.5V, R3.pin_0
