# Fritzing sketch a3Initial (saved by Fritzing 0.9.3b)
breadboards: 1

parts:
  Part2 = Arduino Uno (Rev3)
  LED2 = LED - 5mm [color="Red (633nm)" package="5 mm [THT]"]
  R4 = Resistor [tolerance=±5% resistance=1k package=THT]
  R5 = Resistor [tolerance=±5% resistance=2.2k package=THT]
  R6 = Photocell (LDR) [package=THT]
  LED3 = LED - 5mm [color="Red (633nm)" package="5 mm [THT]"]
  R7 = Resistor [tolerance=±5% resistance=1k package=THT]

nets:
  N1: Part2.A0, R5.Pin_0, R6.pin_1
  N2: Part2.D9_PWM, LED2.cathode, R4.Pin_0, R4.Pin_1
  N3: Part2.D11_PWM/MOSI, LED3.cathode, R7.Pin_0, R7.Pin_1
  N4: Part2.5V, R6.pin_0
  N5: Part2.GND, R5.Pin_1, LED3.anode
