# Fritzing sketch a3copy (saved by Fritzing 0.9.3b)
breadboards: 1

parts:
  Part2 = Arduino Uno (Rev3)
  RED_LED = LED - 5mm [color="Red (633nm)" package="5 mm [THT]"]
  R4 = Resistor [tolerance=±5% resistance=1k package=THT]
  Photoresistor = Photocell (LDR) [package=THT]
  Green_LED = LED - 5mm [color="Green (565nm)" package="5 mm [THT]"]
  R7 = Resistor [tolerance=±5% resistance=1k package=THT]
  R8 = Resistor [tolerance=±5% resistance=2.2k package=THT]

nets (from the schematic view):
  N1: Part2.A0, Photoresistor.pin_0, R8.Pin_0
  N2: Part2.D9_PWM, R4.Pin_1
  N3: Part2.D11_PWM/MOSI, R7.Pin_1
  N4: Part2.GND, RED_LED.cathode, Green_LED.cathode, R8.Pin_1
  N5: Part2.5V, Photoresistor.pin_1
  N6: RED_LED.anode, R4.Pin_0
  N7: Green_LED.anode, R7.Pin_0
